# Fritzing sketch Pollutiton_Fritzing (saved by Fritzing 0.9.3b)
breadboards: 1

parts:
  Composant1 = Arduino Nano (Rev3.0)
  J1 = female pin header, 6 pins [form="♀ (female)"]
  J2 = double row female pin header, 10 pins [form="♀ (female)"]
  C1 = Electrolytic Capacitor [capacitance=0.1mF package="100 mil [THT, electrolytic]"]
  R2 = Resistor [tolerance=±5% resistance=150 package=THT]

nets:
  N1: Composant1.GND, J1.pin2, J1.pin4, J2.pin4, J2.pin10, C1.+, R2.Pin_0
  N2: Composant1.D8, J1.pin3
  N3: Composant1.D10, J2.pin2
  N4: Composant1.D11/MOSI, J2.pin3
  N5: Composant1.D12/MISO, J2.pin7
  N6: Composant1.5V, J1.pin6, J2.pin1
  N7: Composant1.A0, J1.pin5
  N8: Composant1.D13/SCK, J2.pin8
  N9: J1.pin1, C1.-, R2.Pin_1
